# Fritzing sketch SmartWorkPlace (saved by Fritzing 0.9.1b)
circuit board: 8.46667cm x 5.64444cm
breadboards: 1

parts:
  Часть1 = Arduino Uno (Rev3)
  R1 = Photocell (LDR) [package=THT]
  R2 = Resistor [tolerance=±5% resistance=220 package=THT]
  R3 = Resistor [tolerance=±5% resistance=220 package=THT]
  R4 = Temperature Sensor (Thermistor) [thermistor_type=NTC package=THT]
  S1 = Pushbutton [package="[THT]"]
  S2 = Pushbutton [package="[THT]"]
  LCD1 = LCD screen  # not connected
  LED1 = RGB LED (com. cathode, rgb) [package="5 mm [THT]"]
  R5 = Resistor [tolerance=±5% resistance=220 package=THT]
  R6 = Resistor [tolerance=±5% resistance=220 package=THT]
  R7 = Resistor [tolerance=±5% resistance=220 package=THT]

nets:
  N1: Часть1.A0, R3.Pin_1, R4.pin_0
  N2: Часть1.A1, R1.pin_1, R2.Pin_0
  N3: Часть1.GND, R2.Pin_1, R4.pin_1, S1.Pin_3, S1.Pin_4, S2.Pin_3, S2.Pin_4, LED1.common_cathode
  N4: Часть1.D2, LED1.green_anode, R7.Pin_0, R7.Pin_1
  N5: Часть1.D3_PWM, R6.Pin_1
  N6: Часть1.D5_PWM, R5.Pin_0
  N7: Часть1.D6_PWM, S2.Pin_1, S2.Pin_2
  N8: Часть1.D7, S1.Pin_1, S1.Pin_2
  N9: Часть1.5V, R1.pin_0, R3.Pin_0
  N10: LED1.red_anode, R5.Pin_1
  N11: LED1.blue_anode, R6.Pin_0

// code stored in the sketch: sketch_jan11a.ino
#define thermoPin A0
#define lightPin A1
#define thermoKey 7
#define lightKey 6
#define redled 5
#define blueled 2 
#define greenled 3

#include <LiquidCrystal.h>
#include <math.h>

/*

int convArr[8] = {0x16,0x2b,0x3b,0x4b,0x16,0x56,0x8b,0x97};

int symbolConversion(char str) {
  boolean change = false;
  int res;
  for(int i =0;i<sizeof(refArr);i++) {
     if(str==refArr[i]) { 
       change = true;
       res = i; 
       break; 
     }
  }
  if(change)  return res; 
  else return false; 
}
*/
LiquidCrystal lcd(13,12,11,10,9,8);
String valueStorage = "Please enter";
unsigned long thermoWait = millis();
unsigned long lightWait = millis();

void setup() {
  // Initialize pins
  pinMode(thermoPin, INPUT);
  pinMode(lightPin, INPUT);
  pinMode(thermoKey, INPUT_PULLUP);
  pinMode(lightKey, INPUT_PULLUP);
  pinMode(redled, OUTPUT);
  pinMode(blueled, OUTPUT);
  pinMode(greenled, OUTPUT);
  

  //Initialize lcd
  lcd.begin(5, 2);
  lcd.print("Please enter");
  lcd.setCursor(0,1);
  lcd.print("your text!");
  //Initialize serial connection 
  Serial.begin(9600);
}

void loop(){
  
  
  analogWrite(redled, 0);
  analogWrite(blueled, 0);
  digitalWrite(greenled, LOW);

  char incomingChar;
  String valueRead = "";

  //Read the button state
  boolean thermoKeyPressed = digitalRead(thermoKey);
  boolean lightKeyPressed = digitalRead(lightKey);

  //Temperature calculation
  float thermoValue = analogRead(thermoPin)*5.0 / 1023.0;
  float temperature = 1.0 / (log(thermoValue / 2.5) / 4300.0 + 1.0 / 298.0) - 273;
  //Lighting calculation
  float lightValue = 5.0 * (analogRead(lightPin) / 1024.0);
  float  resistor = (10.0*5.0)/lightValue-10.0;
  float  lx = 2223.35*pow(resistor,-10/8);
    char charBufT[25];
    String strT = "temp = ";
    strT+= temperature;
    strT.toCharArray(charBufT, strT.length());
    
    char charBufL[25];
    String strL = "lx = ";
    strL+= lx;
    strL.toCharArray(charBufL, strL.length());
    
    Serial.println(strT);
    Serial.println(strL);

  if(!thermoKeyPressed) {
    //   In case if the key is pressed temperature information is closed
    lcd.clear();
    lcd.print("The temp is");
    lcd.setCursor(0,1);
    lcd.print(temperature);

    delay(3000);
  } 
  else if(!lightKeyPressed) {

    lcd.clear();
    lcd.print("The light is");
    lcd.setCursor(0,1);
    lcd.print(lx);
    delay(3000);
  }
  else {
    //In case  if not pressed works by showing the value recieved from Serial
    while(Serial.available()) {
      incomingChar = Serial.read();
      valueRead.concat(incomingChar);
      Sreial.println(incomingChar)
    }

    if(valueRead!="") {
      valueStorage = valueRead;
      lcd.clear();
      //for(int i=0;i<valueRead.length();i++) {
      //  if(symbolConversion(valueRead[i])!=false) {
      //    valueRead[i] = convArr[symbolConversion(valueRead[i])];
      //    Serial.println(valueRead);
      //  }
     // }
      lcd.print(valueRead);

      if(valueRead.length() > 16) { 
        for(int i=0; i < 32; i++)  {
          lcd.scrollDisplayLeft();
          delay(300);
        }

      }
      Serial.println(valueRead);
    } 
    else if(valueRead=="") {
      lcd.clear();
      lcd.print(valueStorage);
      delay(1000);
      if(valueStorage.length() > 16) { 
        for(int i=0; i < 32; i++)  {
          lcd.scrollDisplayLeft();
          delay(300);
        }

      }
    }

    if((temperature > 28.0) && (millis() > thermoWait)) {
      lcd.clear();
      lcd.print("It's too hot!");
      lcd.setCursor(0,1);
      lcd.print("Turn on the fan.");
      analogWrite(redled,255);
      analogWrite(blueled, 100);
      delay(2000);
      thermoWait = millis()+900000;     
    } 
    else if ((temperature < 22.0) && (millis() > thermoWait)) {
      lcd.clear();
      lcd.print("It's very cold!");
      lcd.setCursor(0,1);
      lcd.print("Let's dance.");
      analogWrite(redled,100);
      analogWrite(blueled, 255);      
      delay(2000);
      thermoWait = millis()+900000;    
    }
    if((lx > 500.0) && (millis() > lightWait)) {
      lcd.clear();
      lcd.print("Too much light!");
      analogWrite(redled,255);
      analogWrite(blueled, 150);
      delay(2000);
      lightWait = millis()+900000;     
    } 
    else if ((lx < 300.0) && (millis() > lightWait)) {
      lcd.clear();
      lcd.print("Too dark!");
      //analogWrite(redled,250);
     // analogWrite(blueled, 150);
      digitalWrite(greenled, HIGH);
      delay(2000);    
      lightWait = millis()+900000;
    }    
  }
}
